# Fritzing sketch heater_safety (saved by Fritzing 0.9.4)
breadboards: 1

parts:
  Q1 = TRANSISTOR_NPN [package=to-92-ammo]
  U1 = Sharp PC817 [package=THT]
  R1 = Resistor [tolerance=±5% resistance=10k package=THT]
  S1 = Round Pushbutton
  R2 = Resistor [tolerance=±5% resistance=1k package=THT]

nets:
  GND: Q1.E, S1.leg0
  N1: Q1.B, R1.Pin_1
  N2: Q1.C, U1.Pin_2
  WRITE: U1.Pin_1
  READ: R1.Pin_0, S1.leg1, R2.Pin_0
  3.3V: R2.Pin_1
