# Fritzing sketch monsoon_esp32devkit (saved by Fritzing 1.0.6)
stripboards: 1

parts:
  M1 = DOIT Esp32 DevKit v1 (30 pins long, 11 pins width) [part_number=ESP32S-PIN30]
  Q1 = npn-Powertransistor [package="TO220 [THT]"]  # not connected
  Q2 = npn-Powertransistor [package="TO220 [THT]"]  # not connected
  R1 = Resistor [tolerance=±5% resistance=220 power=0.25W package=THT]  # not connected
  R2 = Resistor [tolerance=±5% resistance=220 power=0.25W package=THT]  # not connected
  IC2 = Voltage Regulator [package=78xxl]  # not connected
  Part1 = Bluetooth HC-05 Macho  # not connected
  J5 = female pin header, 4 pins [form="♀ (female)"]  # not connected
  J6 = female pin header, 15 pins [form="♀ (female)"]
  J7 = female pin header, 15 pins [form="♀ (female)"]
  J8 = female pin header, 4 pins [form="♀ (female)"]
  J9 = screw terminal, 20 pins
  J10 = screw terminal, 20 pins
  R3 = Resistor [tolerance=±5% power=0.25W resistance=3.3k package=THT]
  R4 = Resistor [tolerance=±5% power=0.25W resistance=3.3k package=THT]
  R5 = Resistor [tolerance=±5% power=0.25W resistance=3.3k package=THT]
  R7 = Resistor [tolerance=±5% power=0.25W resistance=3.3k package=THT]
  R8 = Resistor [tolerance=±5% power=0.25W resistance=15k package=THT]

nets:
  N1: M1.3V3, J7.pin15, J9.pin1, J9.pin18, J9.pin19, J10.pin2, J10.pin20, R3.Pin_1, R4.Pin_1, R5.Pin_0, R7.Pin_0, R8.Pin_0
  N2: M1.GND, J6.pin14, J7.pin14, J8.pin3, J9.pin2, J9.pin14, J9.pin17, J10.pin4, J10.pin19
  N3: M1.D15, J7.pin13, J9.pin16
  N4: M1.D2, J7.pin12, J9.pin7
  N5: M1.D4, J7.pin11, J9.pin6
  N6: M1.RX2, J7.pin10, J8.pin2, J9.pin13
  N7: M1.TX2, J7.pin9, J8.pin1, J9.pin12
  N8: M1.D5, J7.pin8, J9.pin11
  N9: M1.D18, J7.pin7, J9.pin10
  N10: M1.D19, J7.pin6, J9.pin9
  N11: M1.D21, J7.pin5, J9.pin8
  N12: M1.RX0, J7.pin4
  N13: M1.TX0, J7.pin3
  N14: M1.D22, J7.pin2, J9.pin5
  N15: M1.D23, J7.pin1, J9.pin4
  N16: M1.EN, J6.pin1, J10.pin17
  N17: M1.VP, J6.pin2, J10.pin16, R7.Pin_1
  N18: M1.VN, J6.pin3, J10.pin15, R8.Pin_1
  N19: M1.D34, J6.pin4, J10.pin14, R5.Pin_1
  N20: M1.D35, J6.pin5, J10.pin13
  N21: M1.D32, J6.pin6, J10.pin12
  N22: M1.D33, J6.pin7, J10.pin11
  N23: M1.D25, J6.pin8, J10.pin10, R4.Pin_0
  N24: M1.D26, J6.pin9, J10.pin9, R3.Pin_0
  N25: M1.D27, J6.pin10, J10.pin8
  N26: M1.D14, J6.pin11, J10.pin7
  N27: M1.D12, J6.pin12, J10.pin6
  N28: M1.D13, J6.pin13, J10.pin5
  N29: M1.VIN, J6.pin15, J8.pin4, J9.pin3, J9.pin15, J9.pin20, J10.pin1, J10.pin3, J10.pin18

custom parts:
  DOIT Esp32 DevKit v1 (30 pins long, 11 pins width): The DOIT Esp32 DevKit v1 is one of the development board created by DOIT to evaluate the ESP-WROOM-32 module. It is based on the ESP32 microcontroller that boasts Wifi, Bluetooth, Ethernet and Low Power support all in a single chip. (vanepp) made breadboard work, adjusted pin numbering and labels and reduced size of schematic and cleaned up pcb. This chip is 30pins long (2 x15) and 11 pins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
