# Fritzing sketch monsoon_esp (saved by Fritzing 0.9.4)
stripboards: 1

parts:
  M1 = >Wemos D1 R32  # not connected
  J1 = female pin header, 7 pins [form="♀ (female)"]
  J4 = female pin header, 4 pins [form="♀ (female)"]
  J5 = female pin header, 2 pins [form="♀ (female)"]
  J6 = female pin header, 6 pins [form="♀ (female)"]
  J8 = female pin header, 8 pins [form="♀ (female)"]
  J9 = female pin header, 8 pins [form="♀ (female)"]
  R4 = Resistor [tolerance=±5% resistance=4.7k package="2010 [SMD]"]
  R3 = Resistor [tolerance=±5% resistance=3.3k package="2010 [SMD]"]
  R10 = Resistor [tolerance=±5% resistance=4.7k package="2010 [SMD]"]
  R11 = Resistor [tolerance=±5% resistance=4.7k package="2010 [SMD]"]
  R2 = Resistor [tolerance=±5% resistance=4.7k package="2010 [SMD]"]
  R12 = Resistor [tolerance=±5% resistance=4.7k package="2010 [SMD]"]  # not connected
  R13 = Resistor [tolerance=±5% resistance=4.7k package="2010 [SMD]"]  # not connected
  R14 = Resistor [tolerance=±5% resistance=4.7k package="2010 [SMD]"]  # not connected
  R15 = Resistor [tolerance=±5% resistance=4.7k package="2010 [SMD]"]  # not connected
  R16 = Resistor [tolerance=±5% resistance=4.7k package="2010 [SMD]"]
  U1 = Voltage Regulator - 5V [package="TO220 [THT]"]
  C1 = Electrolytic Capacitor [capacitance=330nF package="0405 [SMD, electrolytic]"]
  C7 = Electrolytic Capacitor [capacitance=100nF package="0405 [SMD, electrolytic]"]
  J10 = female pin header, 6 pins [form="♀ (female)"]

nets:
  N1: J1.pin1, J9.pin6, J9.pin7, U1.GND, C1.-, C7.-, J10.pin3
  N2: J1.pin2, J4.pin1
  N3: J1.pin3, J4.pin2
  N4: J1.pin4, J4.pin3
  N5: J1.pin5, J4.pin4
  N6: J1.pin6, J5.pin1
  N7: J1.pin7, J5.pin2
  N8: J6.pin1, R11.Pin_1
  N9: J6.pin2, R3.Pin_1
  N10: J6.pin3, R4.Pin_1
  N11: J6.pin4, R10.Pin_1
  N12: J6.pin5, R2.Pin_1
  N13: J6.pin6, R16.Pin_1
  N14: J8.pin3, J10.pin4
  N15: J8.pin4, J10.pin5
  N16: J9.pin4, R4.Pin_0, R3.Pin_0, R10.Pin_0, R11.Pin_0, R2.Pin_0, R16.Pin_0
  N17: J9.pin8, U1.input_voltage, C7.+
  N18: U1.output_voltage, C1.+, J10.pin2

custom parts:
  >Wemos D1 R32: Wemos D1 R32 - This board is used with dual-mode Wi-Fi and Bluetooth chips, which is safe, reliable, and scalable to a variety of applications. DC in 5V-12V, 1 analog input(3.2V max input), a Micro USB connection, Compatible with D1 R32=WiFi+bluetooth+UNO
