# Fritzing sketch monsoon_mega (saved by Fritzing 0.9.3b)
stripboards: 5

parts:
  R1 = Resistor upright [tolerance=±5% resistance=220 package=THT]
  Q1 = NPN-Transistor [package="TO92 [THT]"]  # not connected
  L1 = female pin header, 4 pins [form="♀ (female)"]
  R4 = Resistor upright [tolerance=±5% resistance=220 package=THT]
  Q2 = NPN-Transistor [package="TO92 [THT]"]
  R5 = Resistor upright [tolerance=±5% resistance=220 package=THT]
  R6 = Resistor upright [tolerance=±5% resistance=220 package=THT]
  J5 = female pin header, 10 pins [form="♀ (female)"]
  J6 = female pin header, 6 pins [form="♀ (female)"]
  J2 = female pin header, 5 pins [form="♀ (female)"]
  J7 = female pin header, 9 pins [form="♀ (female)"]
  J8 = female pin header, 2 pins [form="♀ (female)"]
  J9 = female pin header, 4 pins [form="♀ (female)"]
  J12 = female pin header, 8 pins [form="♀ (female)"]
  J13 = female pin header, 8 pins [form="♀ (female)"]  # not connected
  F0 = female pin header, 3 pins [form="♀ (female)"]
  F1 = female pin header, 3 pins [form="♀ (female)"]
  J10 = female pin header, 5 pins [form="♀ (female)"]
  J16 = female pin header, 1 pin [form="♀ (female)"]
  F2 = female pin header, 3 pins [form="♀ (female)"]
  F3 = female pin header, 3 pins [form="♀ (female)"]
  U0 = female pin header, 4 pins [form="♀ (female)"]
  U1 = female pin header, 4 pins [form="♀ (female)"]
  T0 = female pin header, 3 pins [form="♀ (female)"]
  J22 = female pin header, 12 pins [form="♀ (female)"]
  J11 = female pin header, 6 pins [form="♀ (female)"]
  J23 = female pin header, 2 pins [form="♀ (female)"]
  L3 = female pin header, 4 pins [form="♀ (female)"]
  Q3 = NPN-Transistor [package="TO92 [THT]"]
  R7 = Resistor upright [tolerance=±5% resistance=220 package=THT]
  R8 = Resistor upright [tolerance=±5% resistance=220 package=THT]
  R9 = Resistor upright [tolerance=±5% resistance=220 package=THT]
  R10 = Resistor upright [tolerance=±5% resistance=220 package=THT]
  Q4 = NPN-Transistor [package="TO92 [THT]"]  # not connected
  R11 = Resistor upright [tolerance=±5% resistance=220 package=THT]
  R12 = Resistor upright [tolerance=±5% resistance=220 package=THT]
  L0 = female pin header, 4 pins [form="♀ (female)"]
  L2 = female pin header, 4 pins [form="♀ (female)"]
  R13 = Resistor upright [tolerance=±5% resistance=220 package=THT]
  R14 = Resistor upright [tolerance=±5% resistance=220 package=THT]
  R15 = Resistor upright [tolerance=±5% resistance=220 package=THT]
  R16 = Resistor upright [tolerance=±5% resistance=220 package=THT]
  R17 = Resistor upright [tolerance=±5% resistance=220 package=THT]
  R18 = Resistor upright [tolerance=±5% resistance=220 package=THT]
  Q5 = NPN-Transistor [package="TO92 [THT]"]  # not connected
  Q6 = NPN-Transistor [package="TO92 [THT]"]
  Q7 = NPN-Transistor [package="TO92 [THT]"]
  Q8 = NPN-Transistor [package="TO92 [THT]"]
  Part1 = Arduino Mega 2560 (Rev3)  # not connected
  J28 = female pin header, 12 pins [form="♀ (female)"]
  R19 = Rotary Potentiometer (Small) [maximum_resistance=100kΩ package=THT]
  LED1 = LED - 5mm [color="Red (633nm)" package="5 mm [THT]"]  # not connected
  LED2 = LED - 5mm [color="Red (633nm)" package="5 mm [THT]"]  # not connected
  LED3 = LED - 5mm [color="Red (633nm)" package="5 mm [THT]"]  # not connected
  LED4 = LED - 5mm [color="Red (633nm)" package="5 mm [THT]"]  # not connected
  S1 = Pushbutton [package="[THT]"]  # not connected
  S2 = Pushbutton [package="[THT]"]  # not connected
  S3 = Pushbutton [package="[THT]"]  # not connected
  S4 = Pushbutton [package="[THT]"]  # not connected
  J29 = female pin header, 3 pins [form="♀ (female)"]
  J30 = female pin header, 2 pins [form="♀ (female)"]
  J31 = female pin header, 2 pins [form="♀ (female)"]
  J32 = female pin header, 2 pins [form="♀ (female)"]
  J33 = female pin header, 2 pins [form="♀ (female)"]
  S5 = Taiway 100-SP-X-T1 SPDT Miniature Toggle Switch [part_number=100-SP-X-T1-0-0-B1-M1 package=THT]
  J34 = female pin header, 2 pins [form="♀ (female)"]
  J35 = female pin header, 2 pins [form="♀ (female)"]
  J36 = female pin header, 2 pins [form="♀ (female)"]
  J37 = female pin header, 2 pins [form="♀ (female)"]
  J38 = female pin header, 2 pins [form="♀ (female)"]
  J41 = female pin header, 6 pins [form="♀ (female)"]
  J40 = screw terminal, 6 pins
  R20 = Resistor [tolerance=±5% resistance=330 package=THT]
  Q13 = npn-Powertransistor [package="TO220 [THT]"]  # not connected
  R21 = Resistor upright [tolerance=±5% resistance=220 package=THT]
  T1 = female pin header, 3 pins [form="♀ (female)"]
  F3_2 = female pin header, 3 pins [form="♀ (female)"]
  F2_2 = female pin header, 3 pins [form="♀ (female)"]
  F1_2 = female pin header, 3 pins [form="♀ (female)"]
  F0_2 = female pin header, 3 pins [form="♀ (female)"]
  L1_2 = female pin header, 4 pins [form="♀ (female)"]
  L0_2 = female pin header, 4 pins [form="♀ (female)"]
  L2_2 = female pin header, 4 pins [form="♀ (female)"]
  L3_2 = female pin header, 4 pins [form="♀ (female)"]
  U1_2 = female pin header, 4 pins [form="♀ (female)"]
  U0_2 = female pin header, 4 pins [form="♀ (female)"]
  T1_2 = female pin header, 3 pins [form="♀ (female)"]
  T0_2 = female pin header, 3 pins [form="♀ (female)"]

nets:
  N1: R1.Pin_0, L1.pin3
  N2: R1.Pin_1, L1.pin4, R4.Pin_1, Q2.E, J9.pin2, L3.pin4, Q3.E, R8.Pin_1, R10.Pin_1, R11.Pin_1, R12.Pin_1, L0.pin4, L2.pin4, R14.Pin_1, R18.Pin_1, Q6.E, Q7.E, Q8.E
  N3: L1.pin1, R5.Pin_0, R6.Pin_0, J9.pin1, F0.pin1, F1.pin1, F2.pin3, F3.pin3, U0.pin1, U1.pin1, T0.pin1, J22.pin3, L3.pin1, R7.Pin_0, R9.Pin_0, L0.pin1, L2.pin1, R13.Pin_0, R15.Pin_0, R16.Pin_0, R17.Pin_0, J28.pin3, R19.leg2, J29.pin3, R21.Pin_0, T1.pin1
  N4: L1.pin2, R4.Pin_0, Q2.B
  N5: Q2.C, R6.Pin_1
  N6: J5.pin1, J6.pin1, J7.pin1
  N7: J5.pin2, J7.pin2
  N8: J5.pin3, J7.pin3
  N9: J5.pin4, J7.pin4
  N10: J5.pin5, J7.pin5
  N11: J5.pin6, J7.pin6
  N12: J5.pin7, J7.pin7
  N13: J5.pin8, J7.pin8
  N14: J5.pin9, J7.pin9
  N15: J5.pin10, J6.pin6, J2.pin5
  N16: J6.pin2, J2.pin1
  N17: J6.pin3, J2.pin2
  N18: J6.pin4, J2.pin3
  N19: J6.pin5, J2.pin4
  N20: J8.pin1, J9.pin3, F0.pin3, F1.pin3, F2.pin1, F3.pin1, U0.pin4, U1.pin4, T0.pin3, J22.pin2, J23.pin2, J28.pin2, R19.leg1, J29.pin1, J30.pin2, J31.pin2, J32.pin2, J33.pin2, S5.COM, J34.pin2, J35.pin1, J36.pin1, J37.pin1, J38.pin1, T1.pin3
  N21: J8.pin2, J9.pin4
  N22: J12.pin1, J12.pin2, J22.pin4, J22.pin5, J28.pin4, J28.pin5, J35.pin2, J36.pin2
  N23: J12.pin3, J22.pin6, J28.pin6, J38.pin2
  N24: J12.pin4, J22.pin7, J28.pin7, J37.pin2
  N25: J12.pin5, J22.pin8, J28.pin8, R20.Pin_0
  N26: J12.pin6, J12.pin7, J22.pin9, J22.pin10, J28.pin9, J28.pin10, J31.pin1, J32.pin1
  N27: J12.pin8, J22.pin11, J28.pin11, J33.pin1
  N28: F0.pin2, J10.pin5
  N29: F1.pin2, J10.pin4
  N30: J10.pin1, T0.pin2, R21.Pin_1, T1.pin2
  N31: J10.pin2, F3.pin2
  N32: J10.pin3, F2.pin2
  N33: J16.pin1, J22.pin12, J28.pin12, R19.wiper, J29.pin2
  N34: U0.pin2, J11.pin5
  N35: U0.pin3, J11.pin6
  N36: U1.pin2, J11.pin3
  N37: U1.pin3, J11.pin4
  N38: J22.pin1, J23.pin1, J28.pin1, S5.L2, J34.pin1
  N39: L3.pin2, R10.Pin_0
  N40: L3.pin3, R8.Pin_0
  N41: Q3.B, L2.pin3, R14.Pin_0
  N42: Q3.C, R15.Pin_1
  N43: R11.Pin_0, L0.pin2, Q8.B
  N44: R12.Pin_0, L0.pin3, Q7.B
  N45: L2.pin2, R18.Pin_0, Q6.B
  N46: R13.Pin_1, Q7.C
  N47: R16.Pin_1, Q8.C
  N48: R17.Pin_1, Q6.C
  N49: J30.pin1, R20.Pin_1
  N50: J41.pin1, J40.pin4
  N51: J41.pin2, J40.pin5
  N52: J41.pin3, J40.pin6
  N53: J41.pin4, J41.pin5
  N54: J41.pin6, J40.pin3
  N55: F3_2.pin1, F2_2.pin1
  N56: F3_2.pin2, F2_2.pin2
  N57: F3_2.pin3, F2_2.pin3
  N58: F1_2.pin1, F0_2.pin1
  N59: F1_2.pin2, F0_2.pin2
  N60: F1_2.pin3, F0_2.pin3
  N61: L1_2.pin1, L0_2.pin1
  N62: L1_2.pin2, L0_2.pin2
  N63: L1_2.pin3, L0_2.pin3
  N64: L1_2.pin4, L0_2.pin4
  N65: L2_2.pin1, L3_2.pin1
  N66: L2_2.pin2, L3_2.pin2
  N67: L2_2.pin3, L3_2.pin3
  N68: L2_2.pin4, L3_2.pin4
  N69: U1_2.pin1, U0_2.pin1
  N70: U1_2.pin2, U0_2.pin2
  N71: U1_2.pin3, U0_2.pin3
  N72: U1_2.pin4, U0_2.pin4
  N73: T1_2.pin1, T0_2.pin1
  N74: T1_2.pin2, T0_2.pin2
  N75: T1_2.pin3, T0_2.pin3

custom parts:
  Resistor upright: A generic upright standing resistor (0.25W)
