# Fritzing sketch monsoon_mega2 (saved by Fritzing 0.9.3b)
stripboards: 4

parts:
  J5 = female pin header, 10 pins [form="♀ (female)"]
  J8 = female pin header, 2 pins [form="♀ (female)"]
  J12 = female pin header, 8 pins [form="♀ (female)"]
  J13 = female pin header, 8 pins [form="♀ (female)"]
  J11 = female pin header, 6 pins [form="♀ (female)"]
  Part1 = Arduino Mega 2560 (Rev3)  # not connected
  J28 = female pin header, 12 pins [form="♀ (female)"]
  R19 = Rotary Potentiometer (Small) [maximum_resistance=100kΩ package=THT]
  LED1 = LED - 5mm [color="Red (633nm)" package="5 mm [THT]"]  # not connected
  LED2 = LED - 5mm [color="Red (633nm)" package="5 mm [THT]"]  # not connected
  LED3 = LED - 5mm [color="Red (633nm)" package="5 mm [THT]"]  # not connected
  LED4 = LED - 5mm [color="Red (633nm)" package="5 mm [THT]"]  # not connected
  S1 = Pushbutton [package="[THT]"]  # not connected
  S2 = Pushbutton [package="[THT]"]  # not connected
  S3 = Pushbutton [package="[THT]"]  # not connected
  S4 = Pushbutton [package="[THT]"]  # not connected
  J29 = female pin header, 3 pins [form="♀ (female)"]
  J30 = female pin header, 2 pins [form="♀ (female)"]
  J31 = female pin header, 2 pins [form="♀ (female)"]
  J32 = female pin header, 2 pins [form="♀ (female)"]
  J33 = female pin header, 2 pins [form="♀ (female)"]
  S5 = Taiway 100-SP-X-T1 SPDT Miniature Toggle Switch [part_number=100-SP-X-T1-0-0-B1-M1 package=THT]
  J34 = female pin header, 2 pins [form="♀ (female)"]
  J35 = female pin header, 2 pins [form="♀ (female)"]
  J36 = female pin header, 2 pins [form="♀ (female)"]
  J37 = female pin header, 2 pins [form="♀ (female)"]
  J38 = female pin header, 2 pins [form="♀ (female)"]
  J41 = female pin header, 6 pins [form="♀ (female)"]
  J40 = screw terminal, 6 pins
  R20 = Resistor [tolerance=±5% resistance=330 package=THT]
  Q13 = npn-Powertransistor [package="TO220 [THT]"]  # not connected
  J7 = female pin header, 18 pins [form="♀ (female)"]
  J6 = female pin header, 10 pins [form="♀ (female)"]
  J42 = female pin header, 8 pins [form="♀ (female)"]
  J10 = female pin header, 8 pins [form="♀ (female)"]
  J43 = female pin header, 8 pins [form="♀ (female)"]
  J44 = female pin header, 3 pins [form="♀ (female)"]
  J45 = female pin header, 3 pins [form="♀ (female)"]
  J46 = female pin header, 3 pins [form="♀ (female)"]
  J47 = female pin header, 4 pins [form="♀ (female)"]
  J48 = female pin header, 4 pins [form="♀ (female)"]
  J49 = female pin header, 4 pins [form="♀ (female)"]
  R22 = Resistor upright [tolerance=±5% resistance=220 package=THT]
  J50 = female pin header, 6 pins [form="♀ (female)"]
  J9 = female pin header, 5 pins [form="♀ (female)"]
  J22 = female pin header, 10 pins [form="♀ (female)"]
  R24 = Resistor upright [tolerance=±5% resistance=220 package=THT]
  R25 = Resistor upright [tolerance=±5% resistance=220 package=THT]

nets:
  N1: J5.pin1, J7.pin14
  N2: J5.pin2, J7.pin11
  N3: J5.pin8, J7.pin17
  N4: J5.pin9, J7.pin13
  N5: J8.pin1, J12.pin4, J12.pin5, J12.pin6, J12.pin7, J12.pin8, J43.pin1, J43.pin2, J43.pin3, J43.pin4, J43.pin5, J43.pin6, J43.pin7, J43.pin8, J46.pin1, J46.pin2, J46.pin3, J48.pin1, J48.pin2, J48.pin3, J48.pin4, R22.Pin_0, J50.pin3, J9.pin3, J9.pin4, J22.pin3, J22.pin4
  N6: J8.pin2, J9.pin5
  N7: J12.pin1, R24.Pin_0
  N8: J12.pin2, J50.pin5
  N9: J12.pin3, J50.pin6
  N10: J13.pin1, J42.pin1
  N11: J13.pin2, J42.pin2
  N12: J13.pin3, J42.pin3
  N13: J13.pin4, J42.pin4
  N14: J13.pin5, J42.pin5
  N15: J13.pin6, J42.pin6
  N16: J13.pin7, J42.pin7
  N17: J13.pin8, J42.pin8
  N18: J11.pin1, J22.pin5
  N19: J11.pin2, J22.pin6
  N20: J11.pin3, J22.pin7
  N21: J11.pin4, J22.pin8
  N22: J11.pin5, J22.pin9
  N23: J11.pin6, J22.pin10
  N24: J28.pin1, S5.L2, J34.pin1
  N25: J28.pin2, R19.leg1, J29.pin1, J30.pin2, J31.pin2, J32.pin2, J33.pin2, S5.COM, J34.pin2, J35.pin1, J36.pin1, J37.pin1, J38.pin1
  N26: J28.pin3, R19.leg2, J29.pin3
  N27: J28.pin4, J28.pin5, J35.pin2, J36.pin2
  N28: J28.pin6, J38.pin2
  N29: J28.pin7, J37.pin2
  N30: J28.pin8, R20.Pin_0
  N31: J28.pin9, J28.pin10, J31.pin1, J32.pin1
  N32: J28.pin11, J33.pin1
  N33: J28.pin12, R19.wiper, J29.pin2
  N34: J30.pin1, R20.Pin_1
  N35: J41.pin1, J40.pin4
  N36: J41.pin2, J40.pin5
  N37: J41.pin3, J40.pin6
  N38: J41.pin4, J41.pin5
  N39: J41.pin6, J40.pin3
  N40: J7.pin1, J6.pin2
  N41: J7.pin3, J6.pin4
  N42: J7.pin8, J6.pin5
  N43: J7.pin15, J6.pin3
  N44: J7.pin16, J6.pin6
  N45: J7.pin18, J6.pin1
  N46: J10.pin1, J47.pin1
  N47: J10.pin2, J47.pin2
  N48: J10.pin3, J47.pin3
  N49: J10.pin4, J47.pin4
  N50: J10.pin5, J44.pin1, R25.Pin_1
  N51: J10.pin6, J44.pin2
  N52: J10.pin7, J44.pin3
  N53: J45.pin1, J45.pin2, J45.pin3, J49.pin1, J49.pin2, J49.pin3, J49.pin4, J50.pin2, J9.pin2, J22.pin2, R25.Pin_0
  N54: R22.Pin_1, J50.pin4, R24.Pin_1
  N55: J50.pin1, J9.pin1, J22.pin1

custom parts:
  Resistor upright: A generic upright standing resistor (0.25W)
