# Fritzing sketch monsoon_mega3 (saved by Fritzing 0.9.3b)
circuit board: 10.2729cm x 6.4911cm
stripboards: 3

parts:
  J5 = female pin header, 10 pins [form="♀ (female)"]
  J8 = female pin header, 2 pins [form="♀ (female)"]
  J12 = female pin header, 8 pins [form="♀ (female)"]
  J13 = female pin header, 8 pins [form="♀ (female)"]
  Part1 = Arduino Mega 2560 (Rev3)  # not connected
  J6 = female pin header, 10 pins [form="♀ (female)"]
  J48 = female pin header, 4 pins [form="♀ (female)"]
  J49 = female pin header, 4 pins [form="♀ (female)"]
  R22 = Resistor upright [tolerance=±5% resistance=220 package=THT]
  J9 = female pin header, 5 pins [form="♀ (female)"]
  R24 = Resistor upright [tolerance=±5% resistance=220 package=THT]
  J52 = female pin header, 10 pins [form="♀ (female)"]
  J53 = female pin header, 10 pins [form="♀ (female)"]
  C1 = Electrolytic Capacitor [capacitance=1µF package="100 mil [THT, electrolytic]"]
  R27 = Resistor [tolerance=±5% resistance=220 package=THT]
  J22 = female pin header, 2 pins [form="♀ (female)"]
  J57 = female pin header, 2 pins [form="♀ (female)"]
  J42 = female pin header, 4 pins [form="♀ (female)"]
  J54 = female pin header, 6 pins [form="♀ (female)"]
  J50 = female pin header, 6 pins [form="♀ (female)"]
  J7 = female pin header, 18 pins [form="♀ (female)"]
  J10 = female pin header, 7 pins [form="♀ (female)"]
  J68 = female pin header, 18 pins [form="♀ (female)"]
  J69 = female pin header, 2 pins [form="♀ (female)"]
  IC1 = Voltage Regulator [package=78xxl]
  J11 = female pin header, 5 pins [form="♀ (female)"]
  C2 = Electrolytic Capacitor [capacitance=0pF package="100 mil [THT, electrolytic]"]

nets:
  N1: J5.pin1, J6.pin1, J52.pin1, J53.pin1, J7.pin18, J68.pin18
  N2: J5.pin2, J53.pin2, J7.pin10, J68.pin10
  N3: J5.pin3, J53.pin3, J7.pin11, J68.pin11
  N4: J5.pin4, J53.pin4, J7.pin12, J68.pin12
  N5: J5.pin5, J53.pin5, J7.pin13, J68.pin13
  N6: J5.pin6, J53.pin6, J7.pin14, J68.pin14
  N7: J5.pin7, J53.pin7, J7.pin15, J68.pin15
  N8: J5.pin8, J53.pin8, J7.pin16, J68.pin16
  N9: J5.pin9, J53.pin9, J7.pin17, J68.pin17
  N10: J5.pin10, J53.pin10
  N11: J8.pin1, J49.pin1, J49.pin2, J49.pin3, J49.pin4, R22.Pin_0, J9.pin3, J9.pin4, C1.-
  N12: J8.pin2, J9.pin5
  N13: J12.pin1, R24.Pin_0
  N14: J13.pin1, J42.pin1
  N15: J13.pin2, J42.pin2
  N16: J13.pin3, J42.pin3
  N17: J13.pin4, J42.pin4
  N18: J6.pin2, J52.pin2, J7.pin2, J68.pin2
  N19: J6.pin3, J52.pin3, J7.pin3, J68.pin3
  N20: J6.pin4, J52.pin4, J7.pin4, J68.pin4
  N21: J6.pin5, J52.pin5, J7.pin5, J68.pin5
  N22: J6.pin6, J52.pin6, J7.pin6, J68.pin6
  N23: J6.pin7, J52.pin7, J7.pin7, J68.pin7
  N24: J6.pin8, J52.pin8, J7.pin8, J68.pin8
  N25: J6.pin9, J52.pin9, J7.pin9, J68.pin9
  N26: J6.pin10, J52.pin10
  N27: J48.pin1, J48.pin2, J48.pin3, J48.pin4, J9.pin2, R27.Pin_0
  N28: R22.Pin_1, R24.Pin_1
  N29: C1.+, R27.Pin_1, J11.pin1
  N30: J22.pin1, J11.pin4
  N31: J22.pin2, J11.pin5
  N32: J57.pin1, J10.pin5
  N33: J57.pin2, J10.pin6
  N34: J54.pin1, J50.pin1
  N35: J54.pin2, J50.pin2
  N36: J54.pin3, J50.pin3
  N37: J54.pin4, J50.pin4
  N38: J54.pin5, J50.pin5
  N39: J54.pin6, J50.pin6
  N40: J7.pin1, J68.pin1
  N41: J69.pin1, IC1.IN, C2.+
  N42: J69.pin2, IC1.GND, C2.-

custom parts:
  Resistor upright: A generic upright standing resistor (0.25W)
