# Fritzing sketch scavenge_level (saved by Fritzing 0.9.3b)
stripboards: 1

parts:
  Q14 = NPN-Transistor [package="TO92 [THT]"]
  Part1 = Arduino Uno (Rev3) - ICSP  # not connected
  J42 = female pin header, 3 pins [form="♀ (female)"]
  J43 = female pin header, 2 pins [form="♀ (female)"]
  Q15 = NPN-Transistor [package="TO92 [THT]"]
  R26 = Resistor upright [tolerance=±5% resistance=100k package=THT]
  R27 = Resistor upright [tolerance=±5% resistance=100k package=THT]
  R28 = Resistor upright [tolerance=±5% resistance=10k package=THT]
  R29 = Resistor upright [tolerance=±5% resistance=1k package=THT]
  R30 = Resistor upright [tolerance=±5% resistance=10k package=THT]
  R31 = Resistor upright [tolerance=±5% resistance=1k package=THT]
  J44 = female pin header, 4 pins [form="♀ (female)"]
  J45 = female pin header, 6 pins [form="♀ (female)"]  # not connected
  J46 = female pin header, 8 pins [form="♀ (female)"]
  Q16 = NPN-Transistor [package="TO92 [THT]"]
  R34 = Resistor upright [tolerance=±5% resistance=1k package=THT]
  D1 = Diode [package=diode-1n4148]

nets:
  N1: Q14.E, Q15.E, R26.Pin_1, R27.Pin_1, J44.pin2, Q16.E
  N2: Q14.B, R27.Pin_0, R29.Pin_1
  N3: Q14.C, J42.pin3, R28.Pin_0, R28.Pin_1, R30.Pin_0, J44.pin1, J46.pin5, D1.C
  N4: J42.pin1, R31.Pin_0
  N5: J42.pin2, R29.Pin_0
  N6: J43.pin1, J44.pin3
  N7: J43.pin2, J44.pin4
  N8: Q15.B, R26.Pin_0, R31.Pin_1
  N9: Q15.C, R30.Pin_1, J46.pin6
  N10: J46.pin1, R34.Pin_1
  N11: Q16.B, R34.Pin_0

custom parts:
  Resistor upright: A generic upright standing resistor (0.25W)
